# Fritzing sketch pluto_prototype (saved by Fritzing 1.0.1rc)
breadboards: 1

parts:
  M1 = gear-motor
  M2 = gear-motor
  8-Channel_Relay1 = 8-Channel 5v Relay Shield [package=relay-8ch5v10a]
  Mod3 = Raspberry Pi Pico
  Bauteil1 = Adafruit VL53L0X Time of Flight Distance Sensor [part_number="Adafruit #3317"]
  Bauteil2 = Adafruit VL53L0X Time of Flight Distance Sensor [part_number="Adafruit #3317"]
  Bauteil3 = Adafruit VL53L0X Time of Flight Distance Sensor [part_number="Adafruit #3317"]
  Bauteil4 = Adafruit VL53L0X Time of Flight Distance Sensor [part_number="Adafruit #3317"]
  Bauteil5 = MCP9808 High Accuracy I2C Temperature Sensor [part_number=1782]
  Bauteil6 = MCP9808 High Accuracy I2C Temperature Sensor [part_number=1782]
  A1 = NEO-6M GPS Module [part_number=GY-GPS6MV2]
  S1 = Momentary Switch [package=ksa_sealed_tac_switch]
  M6 = RioRand LM2596
  M7 = RioRand LM2596
  M8 = MDD10A
  Bauteil7 = Adafruit ADS1115 16Bit I2C ADC [part_number="Adafruit #1085"]
  Bauteil8 = 9-DOF Absolute Orientation IMU Fusion Breakout - BNO055

nets:
  N1: M1.pin_1, M8.M1A1
  N2: M1.pin_2, M8.M1B-1
  N3: M2.pin_1, M8.M2B-1
  N4: M2.pin_2, M8.M2A-1
  N5: 8-Channel_Relay1.VCC, M6.Pin_3
  GND: 8-Channel_Relay1.GND, Mod3.pin_3, Mod3.pin_8, Mod3.pin_13, Mod3.pin_18, Mod3.pin_23, Mod3.pin_28, Mod3.pin_33, Mod3.pin_38, Bauteil1.GND, Bauteil2.GND, Bauteil3.GND, Bauteil4.GND, Bauteil5.GND, Bauteil6.GND, A1.GND, M6.Pin_4, M7.Pin_4, M8.GND, Bauteil7.GND, Bauteil8.GND
  N6: 8-Channel_Relay1.IN1, Mod3.pin_12
  N7: 8-Channel_Relay1.IN2, Mod3.pin_11
  N8: 8-Channel_Relay1.IN3, Mod3.pin_10
  N9: 8-Channel_Relay1.IN4, Mod3.pin_9
  N10: 8-Channel_Relay1.IN5, Mod3.pin_7
  N11: 8-Channel_Relay1.IN6, Mod3.pin_6
  N12: 8-Channel_Relay1.IN7, Mod3.pin_5
  N13: 8-Channel_Relay1.IN8, Mod3.pin_4
  N14: Mod3.pin_1, A1.Tx
  N15: Mod3.pin_2, A1.Rx
  N16: Mod3.pin_14, Bauteil8.RST_5V
  N17: Mod3.pin_15, M8.DIR1
  N18: Mod3.pin_16, M8.DIR2
  N19: Mod3.pin_19, M8.PWM1
  N20: Mod3.pin_20, M8.PWM2
  N21: Mod3.pin_21, Bauteil1.SDA, Bauteil2.SDA, Bauteil3.SDA, Bauteil4.SDA, Bauteil5.SDA, Bauteil6.SDA, Bauteil7.SDA, Bauteil8.SDA_5V
  N22: Mod3.pin_22, Bauteil1.SCL, Bauteil2.SCL, Bauteil3.SCL, Bauteil4.SCL, Bauteil5.SCL, Bauteil6.SCL, Bauteil7.SCL, Bauteil8.SCL_5V
  N23: Mod3.pin_24, Bauteil3.XSHUT
  N24: Mod3.pin_25, Bauteil3.GPIO
  N25: Mod3.pin_26, Bauteil2.GPIO
  N26: Mod3.pin_27, Bauteil2.XSHUT
  N27: Mod3.pin_29, Bauteil1.GPIO
  N28: Mod3.pin_30, Bauteil1.XSHUT
  N29: Mod3.pin_31, S1.2
  N30: Mod3.pin_32, Bauteil7.ALERT
  VIN: Bauteil1.VIN, Bauteil2.VIN, Bauteil3.VIN, Bauteil4.VIN, Bauteil5.VDD, Bauteil6.VDD, A1.Vcc, S1.1, M7.Pin_3, Bauteil7.VDD, Bauteil8.5.0V

notes:
  There are just two temperature sensors connected.
  Provide slots for up to 8 sensors!
  OUT: 3.3Volt
  OUT: 5Volt
  ADS1115 to connect 4 16-bit ADC channels.
  For the ADC channels use a voltage divider with 2 47kOhm resistors so voltage is shifted from 0-4.2 Volt to 0-2.1 Volt
  - Connector for Cytron MDD10A Motordriver
  - Connector for 8 Relay module
  - Connector for emergency switch
  - Connector for GPS module
  - Connector for compass module
  - Connectors for 4 distance sensors
  - Connectors for 8 temperature sensors (or other I2C sensors)
  - ON-BOARD LM2596 5V & 3.3V power supply
  - ON-BOARD ADS1115 with voltage dividers for A0/A1/A2/A3

custom parts:
  8-Channel 5v Relay Shield: 8 Channel 5v Relay Shield w. 2x SPD-06VDC-SD-C
  Raspberry Pi Pico: Raspberry Pi Pico. Based around the RP2040 microcontroller the Pico is a low cost microcontroller device bringing Raspberry Pi quality, cost, and easy of use to the microcontroller space. Jan 2021, Split part in to two versions: tht (this one) and SMD. This one will drill holes for a .1 in header in pcb to allow plugging in the module as well as providing pads to solder the module to the top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
  Adafruit VL53L0X Time of Flight Distance Sensor: The VL53L0X is a Time of Flight distance sensor like no other you've used! The sensor contains a very tiny invisible laser source, and a matching sensor. The VL53L0X can detect the "time of flight", or how long the light has taken to bounce back to the sensor. Since it uses a very narrow light source, it is good for determining distance of only the surface directly in front of it. Unlike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
  MCP9808 High Accuracy I2C Temperature Sensor: This I2C digital temperature sensor is one of the more accurate/precise we've ever seen, with a typical accuracy of ±0.25°C over the sensor's -40°C to +125°C range and precision of +0.0625°C. They work great with any microcontroller using standard i2c. There are 3 address pins so you can connect up to 8 to a single I2C bus without address collisions. Best of all, a wide voltage range makes is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
  NEO-6M GPS Module: GY-GPS6MV2 NEO-6M GPS Module Module based on U-blox NEO-6M GPS engine, incorporating regulator for 3.3-5V DC input, MS621FE-compatible rechargeable battery for backup and EEPROM for storing configuration settings. Links: NEO-6 series product information page NEO-6 Datasheet
  Adafruit ADS1115 16Bit I2C ADC: For microcontrollers without an analog-to-digital converter or when you want a higher-precision ADC, the ADS1115 provides 16-bit precision at 860 samples/second over I2C. The chip can be configured as 4 single-ended input channels, or two differential channels. As a nice bonus, it even includes a programmable gain amplifier, up to x16, to help boost up smaller single/differential signals to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
  9-DOF Absolute Orientation IMU Fusion Breakout - BNO055: A MEMS accelerometer, magnetometer and gyroscope on a single die with a high speed ARM Cortex-M0 based processor to digest all the sensor data, abstract the sensor fusion and real time requirements away, and spit out data you can use in quaternions, Euler angles or vectors.
